# Fritzing sketch flowgo (saved by Fritzing 0.9.1b)

parts:
  Part1 = Arduino Uno (Rev3)
  Part2 = Adafruit FONA - Mini Cellular GSM Breakout
  BAT1 = Battery Holders [package=lipo-1100mAh]
  BAT2 = Battery Holders [package=lipo-1100mAh]
  R1 = Photocell (LDR) [package=THT]

nets:
  GND: Part1.GND, Part2.PWRKEY_5V, Part2.GND, BAT1.-, BAT2.-
  N1: Part1.D2, R1.pin_1
  N2: Part1.D3_PWM, Part2.TXD_5V
  N3: Part1.D4, Part2.RESET_5V
  N4: Part1.D5_PWM, Part2.RXD_5V
  N5: Part1.5V, Part2.VCCIO, BAT1.+, R1.pin_0
  N6: Part2.VBAT, BAT2.+

notes:
  Water Flow Sensor
  Micro Hydro Generator

custom parts:
  Adafruit FONA - Mini Cellular GSM Breakout: An all-in-one cellular phone module that lets you add voice, text, SMS and GPRS data to your project. Quad-band 850/900/1800/1900MHz - connect onto any global GSM network with any 2G SIM. Includes an onboard LiPoly battery charging circuitry so you can take your project on the go. Also works as an FM radio receiver.
